# Fritzing sketch Projeto da placa do cubo 3x3x3 (saved by Fritzing 0.8.7b)
circuit board: 10cm x 8cm
breadboards: 1

parts:
  Q1_Nivel_1 = NPN-Transistor [package="TO92 [THT]"]
  Q2_Nivel_2 = NPN-Transistor [package="TO92 [THT]"]
  Q3_Nivel_3 = NPN-Transistor [package="TO92 [THT]"]
  R9 = Resistor [tolerance=±5% resistance=1k package=THT]
  R7 = Resistor [tolerance=±5% resistance=1k package=THT]
  R8 = Resistor [tolerance=±5% resistance=1k package=THT]
  R6 = Resistor [tolerance=±5% resistance=1k package=THT]
  R5 = Resistor [tolerance=±5% resistance=1k package=THT]
  R4 = Resistor [tolerance=±5% resistance=1k package=THT]
  R3 = Resistor [tolerance=±5% resistance=1k package=THT]
  R2 = Resistor [tolerance=±5% resistance=1k package=THT]
  R1 = Resistor [tolerance=±5% resistance=1k package=THT]
  Arduino_Pro_Mini = Arduino Pro Mini v13
  U1 = Voltage Regulator - 5V [package="TO220 [THT]"]
  J1 = Power Jack [package=power_jack_pth_lock]
  Pad1 = Pad [width=5.80647280232283 height=6.42565557719708 connect=center]
  Pad3 = Pad [width=5.80647280232283 height=6.42565557719708 connect=center]
  Pad6 = Pad [width=5.80647280232283 height=6.42565557719708 connect=center]
  Pad8 = Pad [width=5.80647280232283 height=6.42565557719708 connect=center]
  Pad5 = Pad [width=5.80647280232283 height=6.42565557719708 connect=center]
  Pad4 = Pad [width=5.81 height=6.42565557719708 connect=center]
  Pad7 = Pad [width=5.80647280232283 height=6.42565557719708 connect=center]
  Pad2 = Pad [width=5.80647280232283 height=6.42565557719708 connect=center]
  Pad9 = Pad [width=5.80647280232283 height=6.42565557719708 connect=center]
  C1 = Electrolytic Capacitor [capacitance=100nF voltage=10V package="100 mil [THT, electrolytic]"]

nets:
  GND: Q1_Nivel_1.E, Q2_Nivel_2.E, Q3_Nivel_3.E, Arduino_Pro_Mini.GND, U1.GND, J1.GND, J1.GNDBREAK, C1.-
  N1: Q1_Nivel_1.B, Arduino_Pro_Mini.D10_PWM/SS
  N2: Q2_Nivel_2.B, Arduino_Pro_Mini.D11_PWM/MOSI
  N3: Q3_Nivel_3.B, Arduino_Pro_Mini.D12/MISO
  N4: R9.Pin_0, Arduino_Pro_Mini.D9_PWM
  N5: R9.Pin_1, Pad9.pad
  N6: R7.Pin_0, Arduino_Pro_Mini.D7
  N7: R7.Pin_1, Pad7.pad
  N8: R8.Pin_0, Arduino_Pro_Mini.D8
  N9: R8.Pin_1, Pad8.pad
  N10: R6.Pin_0, Arduino_Pro_Mini.D6_PWM
  N11: R6.Pin_1, Pad6.pad
  N12: R5.Pin_0, Arduino_Pro_Mini.D5_PWM
  N13: R5.Pin_1, Pad5.pad
  N14: R4.Pin_0, Arduino_Pro_Mini.D4
  N15: R4.Pin_1, Pad4.pad
  N16: R3.Pin_0, Arduino_Pro_Mini.D3_PWM
  N17: R3.Pin_1, Pad3.pad
  N18: R2.Pin_0, Arduino_Pro_Mini.D2
  N19: R2.Pin_1, Pad2.pad
  N20: R1.Pin_0, Arduino_Pro_Mini.D1/RX
  N21: R1.Pin_1, Pad1.pad
  N22: Arduino_Pro_Mini.VCC, U1.output_voltage, C1.+
  N23: U1.input_voltage, J1.PWR

notes:
  CUBO 3X3X3 BY MAXSON C. M.
